// Logisim project CC162_CPU.circ as structural Verilog: 5 circuits, main circuit main
module main (
);

  wire clk, dipswitch_1_sw1, dipswitch_1_sw2, or_1_out;
  wire [1:0] capcu_1_op_2;
  wire [4:0] ram_1_data_2;
  wire [10:0] capcu_1_op, ram_1_data;
  wire [15:0] A_REG_q, alu_1_alu_out, B_REG_q, C_REG_q, D_REG_q, OUT_REG_q, RAR_q;

  Clock clock_1 (.out(clk));
  Register #(.width(16)) RAR (.D({ram_1_data_2, ram_1_data}), .en(capcu_1_op[10]), .clk(clk), .Q(RAR_q));  // open: clr
  RAM #(.addrWidth(16), .dataWidth(16), .databus("bidir")) ram_1 (
    .addr(RAR_q), .we(capcu_1_op[8]), .oe(capcu_1_op[9]), .clk(clk), .data({ram_1_data_2, ram_1_data}));
  or or_1 (or_1_out, capcu_1_op_2[1], dipswitch_1_sw1);
  Register #(.width(16)) A_REG (
    .D({ram_1_data_2, ram_1_data}), .en(capcu_1_op[0]), .clk(clk), .Q(A_REG_q), .clr(capcu_1_op[4]));
  Register #(.width(16)) B_REG (
    .D({ram_1_data_2, ram_1_data}), .en(capcu_1_op[1]), .clk(clk), .Q(B_REG_q), .clr(capcu_1_op[5]));
  Register #(.width(16)) C_REG (
    .D({ram_1_data_2, ram_1_data}), .en(capcu_1_op[2]), .clk(clk), .Q(C_REG_q), .clr(capcu_1_op[6]));
  Register #(.width(16)) D_REG (
    .D({ram_1_data_2, ram_1_data}), .en(capcu_1_op[3]), .clk(clk), .Q(D_REG_q), .clr(capcu_1_op[7]));
  CAPCU capcu_1 (
    .JMP_VALUE({ram_1_data_2, ram_1_data}), .START(dipswitch_1_sw2), .CLK(clk), .RESET(or_1_out),
    .DATA({ram_1_data_2, ram_1_data}), .OP({capcu_1_op_2, capcu_1_op}));  // open: JMP
  DipSwitch #(.number(2)) dipswitch_1 (.sw1(dipswitch_1_sw1), .sw2(dipswitch_1_sw2));
  ALU alu_1 (
    .A_IN(A_REG_q), .B_IN(B_REG_q), .C_IN(C_REG_q), .D_IN(D_REG_q), .OPCODE(ram_1_data),
    .ALU_OUT(alu_1_alu_out));
  Register #(.width(16)) OUT_REG (
    .D(alu_1_alu_out), .en(ram_1_data_2[0]), .clk(clk), .Q(OUT_REG_q), .clr(ram_1_data_2[1]));
  Hex_Digit_Display hex_digit_display_1 (.value(OUT_REG_q[15:12]));  // open: dp
  Hex_Digit_Display hex_digit_display_2 (.value(OUT_REG_q[11:8]));  // open: dp
  Hex_Digit_Display hex_digit_display_3 (.value(OUT_REG_q[7:4]));  // open: dp
  Hex_Digit_Display hex_digit_display_4 (.value(OUT_REG_q[3:0]));  // open: dp

  // Notes on the sheet:
  //   16 bit data / memory add bus ->
endmodule

module ALU (
  input  [15:0] A_IN,
  input  [15:0] B_IN,
  input  [15:0] C_IN,
  input  [15:0] D_IN,
  input  [10:0] OPCODE,
  output [15:0] ALU_OUT
);

  wire [15:0] au_1_out_au, lu_1_out_lu, multiplexer_1_out, multiplexer_2_out, multiplexer_3_out,
       multiplexer_4_out, not_1_out, not_2_out;

  Multiplexer #(.select(2), .width(16)) multiplexer_1 (
    .in0(A_IN), .in1(B_IN), .in2(C_IN), .in3(D_IN), .out(multiplexer_1_out), .sel(OPCODE[3:2]));
  Multiplexer #(.select(2), .width(16)) multiplexer_2 (
    .in0(A_IN), .in1(B_IN), .in2(C_IN), .in3(D_IN), .out(multiplexer_2_out), .sel(OPCODE[1:0]));
  Multiplexer #(.width(16)) multiplexer_3 (
    .in0(multiplexer_1_out), .in1(not_1_out), .out(multiplexer_3_out), .sel(OPCODE[4]));
  assign not_1_out = ~multiplexer_1_out;  // NOT_Gate not_1, 16 bits wide
  Multiplexer #(.width(16)) multiplexer_4 (
    .in0(multiplexer_2_out), .in1(not_2_out), .out(multiplexer_4_out), .sel(OPCODE[5]));
  assign not_2_out = ~multiplexer_2_out;  // NOT_Gate not_2, 16 bits wide
  AU au_1 (
    .IN_1(multiplexer_3_out), .IN_2(multiplexer_4_out), .OP(OPCODE[9:8]), .OUT_AU(au_1_out_au));  // open: C_REM_OUT, COUT_1
  LU lu_1 (.IN_1(multiplexer_3_out), .IN_2(multiplexer_4_out), .OP(OPCODE[9:8]), .OUT_LU(lu_1_out_lu));
  Multiplexer #(.width(16)) multiplexer_5 (.in0(au_1_out_au), .in1(lu_1_out_lu), .out(ALU_OUT), .sel(OPCODE[10]));
endmodule

module AU (
  input  [15:0] IN_1,
  input  [1:0] OP,
  input  [15:0] IN_2,
  output COUT_1,
  output [15:0] OUT_AU,
  output [15:0] C_REM_OUT
);

  wire adder_1_cout, subtractor_1_bout;
  wire [15:0] adder_1_out, divider_1_out, divider_1_rem, multiplier_1_cout, multiplier_1_out,
       subtractor_1_out;

  Adder #(.width(16)) adder_1 (.a(IN_1), .b(IN_2), .out(adder_1_out), .cout(adder_1_cout));  // open: cin
  Subtractor #(.width(16)) subtractor_1 (
    .a(IN_1), .b(IN_2), .out(subtractor_1_out), .bout(subtractor_1_bout));  // open: bin
  Multiplier #(.width(16)) multiplier_1 (
    .a(IN_1), .b(IN_2), .out(multiplier_1_out), .cout(multiplier_1_cout));  // open: cin
  Divider #(.width(16)) divider_1 (.a(IN_1), .b(IN_2), .out(divider_1_out), .rem(divider_1_rem));  // open: upper
  Multiplexer #(.select(2), .width(16)) multiplexer_1 (
    .in0(adder_1_out), .in1(subtractor_1_out), .in2(multiplier_1_out), .in3(divider_1_out), .out(OUT_AU),
    .sel(OP));
  Multiplexer multiplexer_2 (.in0(adder_1_cout), .in1(subtractor_1_bout), .out(COUT_1), .sel(OP[0]));
  Multiplexer #(.width(16)) multiplexer_3 (.in0(multiplier_1_cout), .in1(divider_1_rem), .out(C_REM_OUT), .sel(OP[1]));
endmodule

module LU (
  input  [15:0] IN_1,
  input  [1:0] OP,
  input  [15:0] IN_2,
  output [15:0] OUT_LU
);

  wire [15:0] and_1_out, or_1_out, xor_1_out;

  assign and_1_out = IN_1 & IN_2;  // AND_Gate and_1, 16 bits wide
  assign or_1_out = IN_1 | IN_2;  // OR_Gate or_1, 16 bits wide
  assign xor_1_out = IN_1 ^ IN_2;  // XOR_Gate xor_1, 16 bits wide
  Multiplexer #(.select(2), .width(16)) multiplexer_1 (
    .in0(and_1_out), .in1(or_1_out), .in2(xor_1_out), .in3(IN_2), .out(OUT_LU), .sel(OP));
endmodule

module CAPCU (
  input  JMP,
  input  [15:0] JMP_VALUE,
  input  START,
  input  CLK,
  input  RESET,
  output [15:0] DATA,
  output [12:0] OP
);

  wire [15:0] counter_1_q;

  ROM #(.addrWidth(16), .dataWidth(29)) rom_1 (.addr(counter_1_q), .data({OP, DATA}));
  Counter #(.max('hffff), .width(16)) counter_1 (
    .load(JMP), .D(JMP_VALUE), .count(START), .Q(counter_1_q), .clk(CLK), .clr(RESET));  // open: carry, up
endmodule
